// Logisim project sum.circ as structural Verilog: 3 circuits, main circuit main
module main (
  input  [3:0] IN_A,
  input  [3:0] IN_B,
  input  IN_CARRY,
  output [3:0] OUT_SUM,
  output OUT_CARRY
);

  wire n2bit_sum_1_out_carry;

  _2bit_sum u_2bit_sum_1 (
    .IN_A(IN_A[1:0]), .IN_B(IN_B[1:0]), .IN_CARRY(IN_CARRY), .OUT_SUM(OUT_SUM[1:0]),
    .OUT_CARRY(n2bit_sum_1_out_carry));
  _2bit_sum u_2bit_sum_2 (
    .IN_A(IN_A[3:2]), .IN_B(IN_B[3:2]), .IN_CARRY(n2bit_sum_1_out_carry), .OUT_SUM(OUT_SUM[3:2]),
    .OUT_CARRY(OUT_CARRY));
endmodule

module bit_sum (
  input  IN_A,
  input  IN_B,
  input  IN_CARRY,
  output OUT_SUM,
  output OUT_CARRY
);

  wire and_1_out, and_2_out, xor_1_out;

  and and_1 (and_1_out, IN_A, IN_B);
  xor xor_1 (xor_1_out, IN_A, IN_B);
  or or_1 (OUT_CARRY, and_1_out, and_2_out);
  and and_2 (and_2_out, xor_1_out, IN_CARRY);
  xor xor_2 (OUT_SUM, xor_1_out, IN_CARRY);
endmodule

module _2bit_sum (
  input  [1:0] IN_A,
  input  [1:0] IN_B,
  input  IN_CARRY,
  output [1:0] OUT_SUM,
  output OUT_CARRY
);

  wire bit_sum_1_out_carry;

  bit_sum bit_sum_1 (
    .IN_A(IN_A[0]), .IN_B(IN_B[0]), .IN_CARRY(IN_CARRY), .OUT_SUM(OUT_SUM[0]), .OUT_CARRY(bit_sum_1_out_carry));
  bit_sum bit_sum_2 (
    .IN_A(IN_A[1]), .IN_B(IN_B[1]), .IN_CARRY(bit_sum_1_out_carry), .OUT_SUM(OUT_SUM[1]),
    .OUT_CARRY(OUT_CARRY));
endmodule
