// Logisim project trafic_light.circ as structural Verilog: 1 circuit, main circuit main
module main (
);

  wire and_1_out, and_2_out, and_3_out, clock_1_out, LOCK_out, or_1_out, or_2_out, or_3_out, or_4_out,
       or_5_out, or_6_out, or_7_out, RST_out, s_r_ff_1_q, s_r_ff_2_q, shift_register_1_out,
       shift_register_1_q0, shift_register_1_q1, shift_register_1_q2, shift_register_2_out,
       shift_register_2_q1, shift_register_2_q3, shift_register_2_q4, UNLOCK_out;

  Shift_Register #(.length(3)) shift_register_1 (
    .in(and_1_out), .clk(clock_1_out), .out(shift_register_1_out), .clr(and_2_out), .q0(shift_register_1_q0),
    .q1(shift_register_1_q1), .q2(shift_register_1_q2));  // open: shift, load, d0, d1, d2
  Clock clock_1 (.out(clock_1_out));
  or or_1 (or_1_out, shift_register_1_q1, shift_register_1_q2, shift_register_1_q0);
  and and_1 (and_1_out, UNLOCK_out, s_r_ff_2_q);
  Button LOCK (.out(LOCK_out));
  Button RST (.out(RST_out));
  or or_2 (or_2_out, RST_out, shift_register_1_out);
  and and_2 (and_2_out, clock_1_out, RST_out);
  or or_3 (or_3_out, RST_out, and_1_out);
  Button UNLOCK (.out(UNLOCK_out));
  and and_3 (and_3_out, LOCK_out, s_r_ff_1_q);
  S_R_Flip_Flop s_r_ff_1 (
    .S(or_2_out), .clk(clock_1_out), .R(and_3_out), .Q(s_r_ff_1_q));  // open: Qn, preset, reset, en
  S_R_Flip_Flop s_r_ff_2 (
    .S(shift_register_2_out), .clk(clock_1_out), .R(or_3_out), .Q(s_r_ff_2_q));  // open: Qn, preset, reset, en
  LED led_1 (.in(or_7_out));
  LED led_2 (.in(or_4_out));
  Shift_Register #(.length(5)) shift_register_2 (
    .in(and_3_out), .clk(clock_1_out), .out(shift_register_2_out), .clr(and_2_out), .q1(shift_register_2_q1),
    .q3(shift_register_2_q3), .q4(shift_register_2_q4));  // open: shift, load, d0, q0, d1, d2, q2, d3, d4
  or or_4 (or_4_out, or_1_out, s_r_ff_2_q);
  LED led_3 (.in(or_5_out));
  or or_5 (or_5_out, s_r_ff_1_q, or_6_out);
  or or_6 (or_6_out, shift_register_2_q3, shift_register_2_q1);
  or or_7 (or_7_out, or_1_out, shift_register_2_q4);
endmodule
